# Fritzing sketch tagreader_esp32_schematics (saved by Fritzing 0.9.3b)

parts:
  Part1 = PN532 Elechouse RFID NFC Module V3
  RGB_SMD_LED1 = SMD RGB LED (WS2812) [package=5050]
  A1 = MH-ET Live Minikit for ESP32
  A2 = buzzer 12mm AT-1224-TWT-5V-2-R

nets:
  GND: Part1.GND, RGB_SMD_LED1.DOut, A1.GND, A2.Pin_2
  VCC: Part1.VCC, RGB_SMD_LED1.VCC, A1.VCC
  N1: Part1.SCL, A1.IO21
  N2: RGB_SMD_LED1.DIn, A1.TDO
  N3: A1.TDI, A2.Pin_1

custom parts:
  PN532 Elechouse RFID NFC Module V3: NFC is a popular technology in recent years. We often heard this work while smart phone company such as Samsung or HTC introduces their latest high-end phones. Almost all the high-end phone in the market support NFC. Near field communication (NFC) is a set of standards for smart phones and similar devices to establish radio communication with each other by touching them together or bringing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
  MH-ET Live Minikit for ESP32: MH-ET Live Minikit for ESP32 ( http://mh.nodebb.com/topic/8/mh-et-live-minikit-for-esp32/2/) PCB footprint is invalid.
  buzzer 12mm AT-1224-TWT-5V-2-R: Buzzer, 87dB, 2400 Hz, 5 V.
